# Fritzing sketch O2_EXP_DHT22 (saved by Fritzing 0.9.3b)
breadboards: 1

parts:
  U1 = Onion Omega2 and Expansion Dock
  RHT1 = Humidity and Temperature Sensor RHT03
  R1 = Resistor [tolerance=±5% resistance=10k package="2010 [SMD]"]

nets:
  N1: U1.GND, RHT1.GND_2
  3.3V: U1.3.3V, RHT1.Vcc, R1.Pin_1
  N2: U1.GPIO19, RHT1.Data-signal, R1.Pin_0

custom parts:
  Onion Omega2 and Expansion Dock: Onion Omega2 IoT Computer on Expansion Dock Omega2: - 580 Mhz MIPS CPU - 64MB RAM, Omega2+: 128MB RAM - 16MB Flash, Omega2+: 32M Flash - LEDE Linux OS - USB2.0 - 2.4GHz b/g/n WiFi - 15GPIO - 2PWM - 2 UART - 1 I2C - 1 SPI - 1 I2S - Micro-SD Card Slot (Omega2+ only) Expansion Dock: - Micro USB Port: Power and USB-to-Serial - USB Type-A Host Port - Reset Button - Power Switch - RGB LED -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
